# Fritzing sketch HW5 (saved by Fritzing 0.9.3b)
breadboards: 1

parts:
  Part1 = Arduino Uno (Rev3)
  LED2 = LED - 3mm [color="Red (633nm)" package="3 mm [THT]"]
  R4 = Basic Flex Resistor
  J1 = Basic Force Sensing Resistor (FSR) [package=THT]
  R3 = Resistor [tolerance=±5% resistance=1k package="0805 [SMD]"]
  R1 = Resistor [tolerance=±5% resistance=18k package="0603 [SMD]"]
  R2 = Resistor [tolerance=±5% resistance=10M package="2512 [SMD]"]

nets:
  N1: Part1.A0, J1.pin_0, R2.Pin_0
  N2: Part1.A1, R4.Pin_2, R1.Pin_0
  N3: Part1.GND, R3.Pin_1, R1.Pin_1
  N4: Part1.D7, LED2.cathode
  N5: Part1.5V, R4.pin_1
  N6: LED2.anode, R3.Pin_0
  N7: J1.pin_1, R2.Pin_1
